// Logisim project Li_Yury_22102550_Pong_project.circ as structural Verilog: 5 circuits, main circuit racketControl
module main (
);

  wire [4:0] A, B;
  wire [23:0] maindesign_1_out_3, maindesign_1_out_4, maindesign_1_out_5, maindesign_1_out_6,
       maindesign_1_out_7, maindesign_1_out_8, maindesign_1_out_9, maindesign_1_out_10, maindesign_1_out_11,
       maindesign_1_out_12, maindesign_1_out_16, maindesign_1_out_17, maindesign_1_out_18,
       maindesign_1_out_19, maindesign_1_out_20, maindesign_1_out_24, maindesign_1_out_25,
       maindesign_1_out_26, maindesign_1_out_27, maindesign_1_out_28, maindesign_1_out_29,
       maindesign_1_out_30, maindesign_1_out_31, maindesign_1_out_32, maindesign_1_out_33,
       maindesign_1_score1a, maindesign_1_score1b, maindesign_1_score2a, maindesign_1_score2b,
       maindesign_1_score3a, maindesign_1_score3b;

  mainDesign maindesign_1 (
    .JoystickA(A), .JoystickB(B), .out_3(maindesign_1_out_3), .out_4(maindesign_1_out_4),
    .out_5(maindesign_1_out_5), .out_6(maindesign_1_out_6), .out_7(maindesign_1_out_7),
    .out_8(maindesign_1_out_8), .out_9(maindesign_1_out_9), .out_10(maindesign_1_out_10),
    .out_11(maindesign_1_out_11), .out_12(maindesign_1_out_12), .Score1A(maindesign_1_score1a),
    .Score2A(maindesign_1_score2a), .Score3A(maindesign_1_score3a), .out_16(maindesign_1_out_16),
    .out_17(maindesign_1_out_17), .out_18(maindesign_1_out_18), .out_19(maindesign_1_out_19),
    .out_20(maindesign_1_out_20), .Score1B(maindesign_1_score1b), .Score2B(maindesign_1_score2b),
    .Score3B(maindesign_1_score3b), .out_24(maindesign_1_out_24), .out_25(maindesign_1_out_25),
    .out_26(maindesign_1_out_26), .out_27(maindesign_1_out_27), .out_28(maindesign_1_out_28),
    .out_29(maindesign_1_out_29), .out_30(maindesign_1_out_30), .out_31(maindesign_1_out_31),
    .out_32(maindesign_1_out_32), .out_33(maindesign_1_out_33));
  Joystick #(.bits(5)) joystick_1 ();  // open: x, y
  DotMatrix #(.matrixcols(31), .matrixrows(24)) dotmatrix_1 (
    .col0(maindesign_1_out_3), .col1(maindesign_1_out_4), .col2(maindesign_1_out_5),
    .col3(maindesign_1_out_6), .col4(maindesign_1_out_7), .col5(maindesign_1_out_8),
    .col6(maindesign_1_out_9), .col7(maindesign_1_out_10), .col8(maindesign_1_out_11),
    .col9(maindesign_1_out_12), .col10(maindesign_1_score1a), .col11(maindesign_1_score2a),
    .col12(maindesign_1_score3a), .col13(maindesign_1_out_16), .col14(maindesign_1_out_17),
    .col15(maindesign_1_out_18), .col16(maindesign_1_out_19), .col17(maindesign_1_out_20),
    .col18(maindesign_1_score1b), .col19(maindesign_1_score2b), .col20(maindesign_1_score3b),
    .col21(maindesign_1_out_24), .col22(maindesign_1_out_25), .col23(maindesign_1_out_26),
    .col24(maindesign_1_out_27), .col25(maindesign_1_out_28), .col26(maindesign_1_out_29),
    .col27(maindesign_1_out_30), .col28(maindesign_1_out_31), .col29(maindesign_1_out_32),
    .col30(maindesign_1_out_33));
  Joystick #(.bits(5)) joystick_2 ();  // open: x, y
endmodule

module racketControl (
  input  [4:0] Joystick,
  input  Lose,
  output [4:0] racket
);

  wire clock_1_out;
  wire [1:0] comparator_1_gt;
  wire [4:0] not_1_out, subtractor_1_out;
  wire [7:0] adder_1_out, bit_extender_1_out, multiplexer_1_out, register_1_q;

  assign not_1_out = ~Joystick;  // NOT_Gate not_1, 5 bits wide
  Subtractor #(.width(5)) subtractor_1 (.a(not_1_out), .b(5'b01111), .out(subtractor_1_out));  // open: bin, bout
  // Probe on subtractor_1_out
  assign bit_extender_1_out = {{3{subtractor_1_out[4]}}, subtractor_1_out};  // Bit_Extender bit_extender_1
  Adder adder_1 (.a(bit_extender_1_out), .b(register_1_q), .out(adder_1_out));  // open: cin, cout
  // Probe on adder_1_out
  Comparator comparator_1 (.a(adder_1_out), .b(8'h48), .gt(comparator_1_gt[0]));  // open: eq, lt
  Comparator comparator_2 (.a(adder_1_out), .b(8'hb8), .lt(comparator_1_gt[1]));  // open: gt, eq
  Multiplexer #(.select(2), .width(8)) multiplexer_1 (
    .in0(adder_1_out), .in1(8'h48), .in2(8'hb8), .out(multiplexer_1_out), .sel(comparator_1_gt));  // open: in3
  Clock clock_1 (.out(clock_1_out));
  Register register_1 (.D(multiplexer_1_out), .en(1'b1), .clk(clock_1_out), .Q(register_1_q), .clr(Lose));
  Adder #(.width(5)) adder_2 (.a(5'b01001), .b(register_1_q[7:3]), .out(racket));  // open: cin, cout
endmodule

module racketDispaly (
  input  Clock,
  input  Lose,
  input  input2,
  input  input1,
  output [4:0] ouput1
);

  wire comparator_1_eq, or_1_out;
  wire [4:0] adder_1_out, multiplexer_1_out, negator_1_out, register_1_q;

  or or_1 (or_1_out, input2, input1);
  Negator #(.width(5)) negator_1 (.in(multiplexer_1_out), .out(negator_1_out));
  Register #(.trigger("falling"), .width(5)) register_1 (
    .D(negator_1_out), .en(or_1_out), .clk(Clock), .Q(register_1_q), .clr(Lose));
  Comparator #(.width(5)) comparator_1 (.a({5{1'b0}}), .b(register_1_q), .eq(comparator_1_eq));  // open: gt, lt
  Multiplexer #(.width(5)) multiplexer_1 (
    .in0(register_1_q), .in1(5'b00001), .out(multiplexer_1_out), .sel(comparator_1_eq));
  Adder #(.width(5)) adder_1 (.a(ouput1), .b(multiplexer_1_out), .out(adder_1_out));  // open: cin, cout
  Register #(.width(5)) register_2 (.D(adder_1_out), .en(1'b1), .clk(Clock), .Q(ouput1), .clr(Lose));
endmodule

module scoreDisplay (
  input  [3:0] Score,
  output [23:0] Score1,
  output [23:0] Score2,
  output [23:0] Score3
);

  wire [14:0] rom_1_data;
  wire [23:0] bit_extender_1_out, bit_extender_2_out, bit_extender_3_out;

  ROM #(.addrWidth(4), .dataWidth(15)) rom_1 (.addr(Score), .data(rom_1_data));
  DotMatrix #(.matrixcols(3), .matrixrows(5)) dotmatrix_1 (
    .col0(rom_1_data[4:0]), .col1(rom_1_data[9:5]), .col2(rom_1_data[14:10]));
  assign bit_extender_1_out = {{19{1'b0}}, rom_1_data[4:0]};  // Bit_Extender bit_extender_1
  assign bit_extender_2_out = {{19{1'b0}}, rom_1_data[9:5]};  // Bit_Extender bit_extender_2
  assign bit_extender_3_out = {{19{1'b0}}, rom_1_data[14:10]};  // Bit_Extender bit_extender_3
  Shifter #(.width(24)) shifter_1 (.in(bit_extender_1_out), .\dist (5'b10010), .out(Score1));
  Shifter #(.width(24)) shifter_2 (.in(bit_extender_2_out), .\dist (5'b10010), .out(Score2));
  Shifter #(.width(24)) shifter_3 (.in(bit_extender_3_out), .\dist (5'b10010), .out(Score3));

  // Notes on the sheet:
  //   contents of rom_1 (hex, n*v repeats v):
  //   7e3f 7c00 76b7 7eb5 7c9c 6ebd 5ebf 7e10 7ebf 7ebd 7ebd
endmodule

module mainDesign (
  input  [4:0] JoystickA,
  input  [4:0] JoystickB,
  output [23:0] out_3,
  output [23:0] out_4,
  output [23:0] out_5,
  output [23:0] out_6,
  output [23:0] out_7,
  output [23:0] out_8,
  output [23:0] out_9,
  output [23:0] out_10,
  output [23:0] out_11,
  output [23:0] out_12,
  output [23:0] Score1A,
  output [23:0] Score2A,
  output [23:0] Score3A,
  output [23:0] out_16,
  output [23:0] out_17,
  output [23:0] out_18,
  output [23:0] out_19,
  output [23:0] out_20,
  output [23:0] Score1B,
  output [23:0] Score2B,
  output [23:0] Score3B,
  output [23:0] out_24,
  output [23:0] out_25,
  output [23:0] out_26,
  output [23:0] out_27,
  output [23:0] out_28,
  output [23:0] out_29,
  output [23:0] out_30,
  output [23:0] out_31,
  output [23:0] out_32,
  output [23:0] out_33
);

  wire and_1_out, and_2_out, and_3_out, Clock, clock_1_out, comparator_1_gt, comparator_2_lt,
       comparator_3_gt, comparator_4_lt, comparator_5_lt, comparator_6_lt, comparator_7_lt, comparator_8_lt,
       comparator_9_eq, comparator_10_eq, comparator_11_eq, Lose, not_1_out, or_1_out, undriven;
  wire [2:0] counter_1_q;
  wire [3:0] adder_3_out, adder_4_out, ScoreA, ScoreB;
  wire [4:0] adder_1_out, adder_2_out, adder_5_out, adder_6_out, adder_7_out, Ay, By, racketdispaly_1_ouput1,
       racketdispaly_2_ouput1;
  wire [23:0] demultiplexer_1_out0, demultiplexer_1_out1, demultiplexer_1_out2, demultiplexer_1_out3,
       demultiplexer_1_out4, demultiplexer_1_out5, demultiplexer_1_out6, demultiplexer_1_out7,
       demultiplexer_1_out8, demultiplexer_1_out9, demultiplexer_1_out10, demultiplexer_1_out11,
       demultiplexer_1_out12, demultiplexer_1_out15, demultiplexer_1_out16, demultiplexer_1_out17,
       demultiplexer_1_out18, demultiplexer_1_out19, demultiplexer_1_out20, demultiplexer_1_out21,
       demultiplexer_1_out22, demultiplexer_1_out23, demultiplexer_1_out24, demultiplexer_1_out25,
       demultiplexer_1_out26, demultiplexer_1_out27, demultiplexer_1_out28, demultiplexer_1_out29,
       demultiplexer_1_out30, scoredisplay_1_score1, scoredisplay_1_score2, scoredisplay_1_score3,
       scoredisplay_2_score1, scoredisplay_2_score2, scoredisplay_2_score3, shifter_1_out, shifter_2_out,
       shifter_3_out;

  Adder #(.width(5)) adder_1 (.a(By), .b(5'b01000), .out(adder_1_out));  // open: cin, cout
  Comparator #(.width(5)) comparator_1 (
    .a(racketdispaly_2_ouput1), .b(5'b01100), .gt(comparator_1_gt));  // open: eq, lt
  Adder #(.width(5)) adder_2 (.a(Ay), .b(5'b01100), .out(adder_2_out));  // open: cin, cout
  Comparator #(.width(5)) comparator_2 (
    .a(racketdispaly_2_ouput1), .b(5'b10100), .lt(comparator_2_lt));  // open: gt, eq
  Comparator #(.width(5)) comparator_3 (
    .a(racketdispaly_1_ouput1), .b(5'b01011), .gt(comparator_3_gt));  // open: eq, lt
  Comparator #(.width(5)) comparator_4 (
    .a(racketdispaly_1_ouput1), .b(5'b10110), .lt(comparator_4_lt));  // open: gt, eq
  Comparator #(.mode("unsigned"), .width(5)) comparator_5 (
    .a(adder_6_out), .b(By), .lt(comparator_5_lt));  // open: gt, eq
  Comparator #(.mode("unsigned"), .width(5)) comparator_6 (
    .a(adder_6_out), .b(adder_1_out), .lt(comparator_6_lt));  // open: gt, eq
  Comparator #(.mode("unsigned"), .width(5)) comparator_7 (
    .a(adder_6_out), .b(Ay), .lt(comparator_7_lt));  // open: gt, eq
  Comparator #(.mode("unsigned"), .width(5)) comparator_8 (
    .a(adder_6_out), .b(adder_2_out), .lt(comparator_8_lt));  // open: gt, eq
  Adder #(.width(4)) adder_3 (.a(ScoreA), .b(4'b0001), .out(adder_3_out));  // open: cin, cout
  or or_1 (or_1_out, Lose, and_1_out);
  and and_1 (and_1_out, clock_1_out, not_1_out);
  Clock clock_1 (.out(clock_1_out));
  and and_2 (and_2_out, ~comparator_5_lt, comparator_6_lt, comparator_1_gt);  // AND_Gate
  and and_3 (and_3_out, ~comparator_7_lt, comparator_8_lt, comparator_2_lt);  // AND_Gate
  Register #(.width(4)) register_1 (
    .D(adder_3_out), .en(comparator_10_eq), .clk(comparator_10_eq), .Q(ScoreA));  // open: clr
  Counter #(.max('h7), .width(3)) counter_1 (
    .load(Lose), .D(3'b110), .Q(counter_1_q), .up(1'b0), .clk(or_1_out));  // open: count, carry, clr
  not not_1 (not_1_out, comparator_9_eq);
  Comparator #(.width(3)) comparator_9 (.a(counter_1_q), .b(3'b000), .eq(comparator_9_eq));  // open: gt, lt
  and and_4 (Clock, ~not_1_out, clock_1_out);  // AND_Gate
  racketControl racketcontrol_1 (.Joystick(JoystickA), .Lose(Lose), .racket(Ay));
  racketControl racketcontrol_2 (.Joystick(JoystickB), .Lose(Lose), .racket(By));
  Shifter #(.width(24)) shifter_1 (.in(24'h3f), .\dist (Ay), .out(shifter_1_out));
  racketDispaly racketdispaly_1 (
    .Clock(Clock), .Lose(Lose), .input2(comparator_3_gt), .input1(comparator_4_lt),
    .ouput1(racketdispaly_1_ouput1));
  Register #(.width(4)) register_2 (
    .D(adder_4_out), .en(comparator_11_eq), .clk(comparator_11_eq), .Q(ScoreB), .clr(undriven));
  Adder #(.width(4)) adder_4 (.a(ScoreB), .b(4'b0001), .out(adder_4_out));  // open: cin, cout
  Shifter #(.width(24)) shifter_2 (.in(24'h3f), .\dist (By), .out(shifter_2_out));
  Adder #(.width(5)) adder_5 (.a(5'b01011), .b(racketdispaly_1_ouput1), .out(adder_5_out));  // open: cin, cout
  racketDispaly racketdispaly_2 (
    .Clock(Clock), .Lose(Lose), .input2(and_2_out), .input1(and_3_out), .ouput1(racketdispaly_2_ouput1));
  Shifter #(.width(24)) shifter_3 (.in(24'h1), .\dist (adder_5_out), .out(shifter_3_out));
  Comparator #(.width(5)) comparator_10 (
    .a(5'b01111), .b(racketdispaly_2_ouput1), .eq(comparator_10_eq));  // open: gt, lt
  Comparator #(.width(5)) comparator_11 (
    .a(5'b10001), .b(racketdispaly_2_ouput1), .eq(comparator_11_eq));  // open: gt, lt
  Adder #(.width(5)) adder_6 (.a(adder_5_out), .b(5'b00001), .out(adder_6_out));  // open: cin, cout
  Demultiplexer #(.select(5), .width(24)) demultiplexer_1 (
    .out0(demultiplexer_1_out0), .out1(demultiplexer_1_out1), .out2(demultiplexer_1_out2),
    .out3(demultiplexer_1_out3), .out4(demultiplexer_1_out4), .out5(demultiplexer_1_out5),
    .out6(demultiplexer_1_out6), .out7(demultiplexer_1_out7), .out8(demultiplexer_1_out8),
    .out9(demultiplexer_1_out9), .out10(demultiplexer_1_out10), .out11(demultiplexer_1_out11),
    .out12(demultiplexer_1_out12), .out13(out_16), .out14(out_17), .out15(demultiplexer_1_out15),
    .out16(demultiplexer_1_out16), .out17(demultiplexer_1_out17), .out18(demultiplexer_1_out18),
    .out19(demultiplexer_1_out19), .out20(demultiplexer_1_out20), .out21(demultiplexer_1_out21),
    .out22(demultiplexer_1_out22), .out23(demultiplexer_1_out23), .out24(demultiplexer_1_out24),
    .out25(demultiplexer_1_out25), .out26(demultiplexer_1_out26), .out27(demultiplexer_1_out27),
    .out28(demultiplexer_1_out28), .out29(demultiplexer_1_out29), .out30(demultiplexer_1_out30),
    .in(shifter_3_out), .sel(adder_7_out));  // open: out31
  Adder #(.width(5)) adder_7 (.a(5'b01111), .b(racketdispaly_2_ouput1), .out(adder_7_out));  // open: cin, cout
  or or_2 (Lose, comparator_10_eq, comparator_11_eq);
  assign out_4 = shifter_1_out | demultiplexer_1_out1;  // OR_Gate or_3, 24 bits wide
  assign out_32 = demultiplexer_1_out30 | shifter_2_out;  // OR_Gate or_4, 24 bits wide
  scoreDisplay scoredisplay_1 (
    .Score(ScoreA), .Score1(scoredisplay_1_score1), .Score2(scoredisplay_1_score2),
    .Score3(scoredisplay_1_score3));
  assign out_5 = demultiplexer_1_out2;  // OR_Gate or_5, 24 bits wide OR_Gate
  assign Score1A = demultiplexer_1_out10 | scoredisplay_1_score1;  // OR_Gate or_6, 24 bits wide
  assign Score2A = demultiplexer_1_out11 | scoredisplay_1_score2;  // OR_Gate or_7, 24 bits wide
  assign Score3A = demultiplexer_1_out12 | scoredisplay_1_score3;  // OR_Gate or_8, 24 bits wide
  assign Score1B = scoredisplay_2_score1 | demultiplexer_1_out18;  // OR_Gate or_9, 24 bits wide
  assign Score2B = scoredisplay_2_score2 | demultiplexer_1_out19;  // OR_Gate or_10, 24 bits wide
  assign Score3B = scoredisplay_2_score3 | demultiplexer_1_out20;  // OR_Gate or_11, 24 bits wide
  assign out_27 = demultiplexer_1_out24;  // OR_Gate or_12, 24 bits wide OR_Gate
  assign out_28 = demultiplexer_1_out25;  // OR_Gate or_13, 24 bits wide OR_Gate
  scoreDisplay scoredisplay_2 (
    .Score(ScoreB), .Score1(scoredisplay_2_score1), .Score2(scoredisplay_2_score2),
    .Score3(scoredisplay_2_score3));
  assign out_3 = {24{1'b0}} | demultiplexer_1_out0;  // OR_Gate or_14, 24 bits wide
  assign out_18 = 24'h555555 | demultiplexer_1_out15;  // OR_Gate or_15, 24 bits wide
  assign out_29 = demultiplexer_1_out26;  // OR_Gate or_16, 24 bits wide OR_Gate
  assign out_6 = demultiplexer_1_out3;  // OR_Gate or_17, 24 bits wide OR_Gate
  assign out_33 = demultiplexer_1_out29 | {24{1'b0}};  // OR_Gate or_18, 24 bits wide
  assign out_7 = demultiplexer_1_out4;  // OR_Gate or_19, 24 bits wide OR_Gate
  assign out_12 = demultiplexer_1_out9;  // OR_Gate or_20, 24 bits wide OR_Gate
  assign out_30 = demultiplexer_1_out27;  // OR_Gate or_21, 24 bits wide OR_Gate
  assign out_31 = demultiplexer_1_out28;  // OR_Gate or_22, 24 bits wide OR_Gate
  assign out_8 = demultiplexer_1_out5;  // OR_Gate or_23, 24 bits wide OR_Gate
  assign out_11 = demultiplexer_1_out8;  // OR_Gate or_24, 24 bits wide OR_Gate
  assign out_19 = demultiplexer_1_out16;  // OR_Gate or_25, 24 bits wide OR_Gate
  assign out_20 = demultiplexer_1_out17;  // OR_Gate or_26, 24 bits wide OR_Gate
  assign out_25 = demultiplexer_1_out22;  // OR_Gate or_27, 24 bits wide OR_Gate
  assign out_24 = demultiplexer_1_out21;  // OR_Gate or_28, 24 bits wide OR_Gate
  assign out_9 = demultiplexer_1_out6;  // OR_Gate or_29, 24 bits wide OR_Gate
  assign out_10 = demultiplexer_1_out7;  // OR_Gate or_30, 24 bits wide OR_Gate
  assign out_26 = demultiplexer_1_out23;  // OR_Gate or_31, 24 bits wide OR_Gate
endmodule
